# Fritzing sketch DachaAlarm (saved by Fritzing 0.9.3b)

parts:
  Part1 = Arduino Uno (Rev3) - ICSP
  R1 = Resistor [tolerance=±5% resistance=10k package=THT]
  S1 = Reed switch [package=THT]
  Sensore_PIR_HC-SR502 = HC-SR501 Body Sensor Module

nets:
  GND: Part1.GND, R1.Pin_0, Sensore_PIR_HC-SR502.GND
  N1: Part1.D2, Sensore_PIR_HC-SR502.OUT
  N2: Part1.D4, R1.Pin_1, S1.pin_2
  5V: Part1.5V, S1.pin_1, Sensore_PIR_HC-SR502.VCC

custom parts:
  HC-SR501 Body Sensor Module: Pyroelectric Infrared PIR Motion Sensor Detector Module
