# Fritzing sketch WaterFloodProtectionSystem (saved by Fritzing 0.9.3b)
breadboards: 3
perfboards: 3

parts:
  Part1 = Arduino Uno (Rev3)
  R5 = Resistor [tolerance=±5% resistance=1k package=THT]
  R6 = Resistor [tolerance=±5% resistance=1k package=THT]
  U3 = mystery part, 2 pins [chip_label=Аквасторож]
  U4 = mystery part, 2 pins [chip_label=Аквасторож]
  R7 = Resistor [tolerance=±5% resistance=10k package=THT]
  R8 = Resistor [tolerance=±5% resistance=10k package=THT]
  R9 = Resistor [tolerance=±5% resistance=1k package=THT]
  LED1 = LED - 5mm [color="Green (565nm)" package="5 mm [THT]"]
  LED2 = LED - 5mm [color="Yellow (595nm)" package="5 mm [THT]"]
  R10 = Resistor [tolerance=±5% resistance=220 package=THT]
  LED4 = LED - 5mm [color="Red (633nm)" package="5 mm [THT]"]
  R11 = Resistor [tolerance=±5% resistance=1k package=THT]
  M1 = DC Motor
  J1 = Screw terminal - 2 pins [package=THT]  # not connected
  J2 = Screw terminal - 2 pins [package=THT]
  S3 = Momentary Switch [package=ksa_sealed_tac_switch]
  S4 = Momentary Switch [package=ksa_sealed_tac_switch]
  R12 = Resistor [tolerance=±5% resistance=1k package=THT]
  R13 = Resistor [tolerance=±5% resistance=1k package=THT]
  R14 = Resistor [tolerance=±5% resistance=1k package=THT]
  LED5 = LED - 3mm [color="Red (633nm)" package="3 mm [THT]"]
  R15 = Resistor [tolerance=±5% resistance=1k package=THT]
  R16 = Resistor [tolerance=±5% resistance=1k package=THT]
  R17 = Resistor [tolerance=±5% resistance=1k package=THT]
  R18 = Resistor [tolerance=±5% resistance=1k package=THT]
  LED6 = LED - 3mm [color="Yellow (595nm)" package="3 mm [THT]"]
  LED7 = LED - 3mm [color="Green (555nm)" package="3 mm [THT]"]
  S2 = Momentary Switch [package=ksa_sealed_tac_switch]
  LED8 = LED - 3mm [color="Green (555nm)" package="3 mm [THT]"]
  R19 = Resistor [tolerance=±5% resistance=1k package=THT]
  R20 = Resistor [tolerance=±5% resistance=1k package=THT]
  R21 = Resistor [tolerance=±5% resistance=10k package=THT]
  R22 = Resistor [tolerance=±5% resistance=10k package=THT]
  U6 = mystery part, 2 pins [chip_label=Аквасторож]
  U7 = mystery part, 2 pins [chip_label=Аквасторож]
  U5 = mystery part, 6 pins [chip_label=L9110]

nets:
  N1: Part1.A0, S4.2, R13.Pin_1, R14.Pin_0
  N2: Part1.D8, Part1.D9_PWM, Part1.D10_PWM/SS, R9.Pin_0, R10.Pin_0, R11.Pin_0
  N3: Part1.D11_PWM/MOSI, U5.pin4
  N4: Part1.D12/MISO, U5.pin3
  N5: Part1.GND, R7.Pin_1, R8.Pin_1, LED1.anode, LED2.anode, LED4.anode, R14.Pin_1, U5.pin2
  N6: Part1.D2, R5.Pin_0, R8.Pin_0
  N7: Part1.D4, R6.Pin_0, R7.Pin_0
  N8: Part1.5V, U3.pin2, U4.pin2, S3.3, S4.3, S2.3, U5.pin1
  N9: R5.Pin_1, U3.pin1
  N10: R6.Pin_1, U4.pin1
  N11: R9.Pin_1, LED1.cathode
  N12: LED2.cathode, R10.Pin_1
  N13: LED4.cathode, R11.Pin_1
  N14: M1.pin_1, J2.pin1
  N15: M1.pin_2, J2.pin2
  N16: S3.2, R12.Pin_1, R13.Pin_0
  N17: R12.Pin_0, S2.2
  N18: LED5.cathode, R17.Pin_0
  N19: LED5.anode, LED6.anode, LED7.anode, LED8.anode
  N20: R15.Pin_0, LED7.cathode
  N21: R16.Pin_1, LED8.cathode
  N22: R18.Pin_1, LED6.cathode
  N23: R19.Pin_0, R21.Pin_1
  N24: R19.Pin_1, U6.pin1
  N25: R20.Pin_0, R22.Pin_1
  N26: R20.Pin_1, U7.pin1
  N27: R21.Pin_0, R22.Pin_0

notes:
  10kΩ
  1kΩ
  Open
  Close
  Reset
  342 for Open
  513 for Close
  1018 for Reset
  square LED
  Cable to motor
